# Fritzing sketch Connections (saved by Fritzing 0.9.3b)
breadboards: 1

parts:
  LED1 = LED - 5mm [color="Red (633nm)" package="5 mm [THT]"]
  R6 = Resistor [tolerance=±5% resistance=560 package="2010 [SMD]"]
  R1 = Rotary Potentiometer (Small) [maximum_resistance=10kΩ package=THT]
  R5 = PHOTOCELL [package=photocell-kit]
  R2 = Rotary Potentiometer (Small) [maximum_resistance=10kΩ package=THT]
  Breakout2 = BMP280 [package=Breakout]
  Raspberry_Pi1 = Raspberry Pi 2
  MCP3008 = IC, DIP package, 16 pins [chip_label=MCP3008 part_number=MCP3008]
  R3 = Resistor [tolerance=±5% resistance=560 package="2010 [SMD]"]
  SENSOR1 = TCS34725 RGB Color Sensor
  Part2 = Arduino Nano (Rev3.0)
  Part3 = NeoPixel Jewel
  IC1 = ULN2003A [package="DIP16 [THT]"]
  M2 = Stepper Motor - Unipolar

nets:
  N1: LED1.cathode, Raspberry_Pi1.GPIO26
  N2: LED1.anode, R6.Pin_0
  VIN: R6.Pin_1, R1.leg2, R5.P$1, R2.leg2, Breakout2.VIN, Raspberry_Pi1.3v3, MCP3008.pin15, MCP3008.pin16, SENSOR1.VDD
  GND: R1.leg1, R2.leg1, Breakout2.GND, Raspberry_Pi1.GND, MCP3008.pin9, MCP3008.pin14, R3.Pin_1, SENSOR1.GND, IC1.0V
  N3: R1.wiper, MCP3008.pin1
  N4: R5.P$2, MCP3008.pin3, R3.Pin_0
  N5: R2.wiper, MCP3008.pin2
  N6: Breakout2.SCK, Raspberry_Pi1.GPIO3, SENSOR1.SCL
  N7: Breakout2.SDI, Raspberry_Pi1.GPIO2, SENSOR1.SDA
  N8: Raspberry_Pi1.GPIO10, MCP3008.pin11
  N9: Raspberry_Pi1.GPIO9, MCP3008.pin12
  N10: Raspberry_Pi1.GPIO11, MCP3008.pin13
  N11: Raspberry_Pi1.GPIO5, IC1.In_4
  N12: Raspberry_Pi1.GPIO6, IC1.In_3
  N13: Raspberry_Pi1.GPIO13, IC1.In_2
  N14: Raspberry_Pi1.GPIO19, IC1.In_1
  N15: Raspberry_Pi1.GPIO8, MCP3008.pin10
  GND_2: Part2.GND, Part3.GND
  N16: Part2.D9, Part3.Data_In
  5V: Part2.5V, Part3.VDD
  N17: IC1.Out_1, M2.A

notes:
  + Power, EXTERNAL, 4 x AA or similar (depend on stepper)
  See also stepper colors / description
  ULN2003A is an array of seven NPN Darlington transistors capable of 500mA, 50V output

custom parts:
  BMP280: Barometric Pressure and Temperature Sensor
  TCS34725 RGB Color Sensor: TCS34725 RGB Color Sensor with LED
  NeoPixel Jewel: Seven of our the tiny 5050 (5mm x 5mm) smart RGB LEDs onto a beautiful, round PCB with mounting holes and a chainable design to create what we think is our most elegant (and evening-wear appropriate) NeoPixel board yet.
