# Fritzing sketch Resitors (saved by Fritzing 0.9.2b)

parts:
  Raspberry_Pi2 = Raspberry Pi 2
  proto1 = Adafruit_PermaProto_1_4_Board
  LED2 = LED - 5mm [color="Yellow (585nm)" package="5 mm [THT]"]  # not connected
  R7 = Resistor [tolerance=±5% resistance=560 package="2010 [SMD]"]  # not connected
  LED3 = LED - 5mm [color="Orange (612nm)" package="5 mm [THT]"]  # not connected
  LED4 = LED - 5mm [color="Blue (525nm)" package="5 mm [THT]"]  # not connected
  R8 = Resistor [tolerance=±5% resistance=560 package="2010 [SMD]"]  # not connected

nets:
  N1: Raspberry_Pi2.3v3, proto1.connectorY2
  N2: Raspberry_Pi2.GPIO13, proto1.connectorB11
  N3: Raspberry_Pi2.GPIO19, proto1.connectorC7
  N4: Raspberry_Pi2.GPIO26, proto1.connectorD4
  N5: Raspberry_Pi2.GND, proto1.connectorZ1
  N6: proto1.connectorE8, proto1.connectorZ8
  N7: proto1.connectorJ3, proto1.connectorY3

notes:
  A B C
